# Fritzing sketch eggfckr_brd-fritzing (saved by Fritzing 0.9.2b)

parts:
  U1 = attiny85 [package=dip]
  LED2 = LED - 3mm [color="Red (633nm)" package="3 mm [THT]"]
  LED3 = LED - 3mm [color="Red (633nm)" package="3 mm [THT]"]
  R2 = Resistor [tolerance=±5% resistance=220 package=THT]
  coin_cell_3V_battary = Battery Holders [package=battcon_12mm]
  U2 = POT [package=pot_alpha_rv16af-20]
  part = Resistor [tolerance=±5% resistance=220 package=THT]

nets:
  N1: U1.Pin_2, part.Pin_1
  N2: U1.Pin_3, U2.S
  GND: U1.Pin_4, coin_cell_3V_battary.-, U2.A
  N3: U1.Pin_7, R2.Pin_1
  3V: U1.Pin_8, LED2.anode, LED3.anode, coin_cell_3V_battary.+, U2.E
  N4: LED2.cathode, part.Pin_0
  N5: LED3.cathode, R2.Pin_0
